// Logisim project Final.circ as structural Verilog: 3 circuits, main circuit Queue
// Evac Queue
module Queue (
  input  [7:0] Zero,
  input  Clear,
  input  Reset,
  input  Main_Clock,
  input  Serve,
  input  Insert,
  input  [7:0] Zone,
  input  [1:0] Priority,
  output Empty,
  output [7:0] Output_Zone,
  output [1:0] out_11
);

  wire and_1_out, and_2_out, and_3_out, and_4_out, and_5_out, decoder_1_out0, decoder_1_out1, decoder_1_out2,
       decoder_1_out3, or_1_out;
  wire [1:0] counter_1_q, counter_3_q, P1_q, P2_q, P3_q, P4_q;
  wire [7:0] counter_2_q, register_1_q, register_2_q, register_3_q, register_4_q;

  and and_1 (and_1_out, Serve, Main_Clock);
  and and_2 (and_2_out, Insert, Main_Clock);
  or or_1 (or_1_out, and_1_out, and_2_out);
  and and_3 (and_3_out, Serve, Main_Clock);
  and and_4 (and_4_out, Insert, Main_Clock);
  Counter #(.width(2), .max('h3)) counter_1 (
    .count(1'b1), .Q(counter_1_q), .clk(and_4_out), .clr(Reset));  // open: load, D, carry
  Counter counter_2 (.load(and_1_out), .count(1'b1), .Q(counter_2_q), .clk(or_1_out), .clr(Clear));  // open: D, carry
  Counter #(.width(2), .max('h3)) counter_3 (
    .Q(counter_3_q), .clk(and_3_out), .clr(Reset));  // open: load, D, count, carry
  Decoder #(.select(2)) decoder_1 (
    .out0(decoder_1_out0), .out1(decoder_1_out1), .out2(decoder_1_out2), .out3(decoder_1_out3),
    .sel(counter_1_q), .en(1'b1));
  and and_5 (and_5_out, Insert, Main_Clock);
  Comparator #(.mode("unsigned")) comparator_1 (.a(Zero), .b(counter_2_q), .eq(Empty));  // open: gt, lt
  Register register_1 (.D(Zone), .en(decoder_1_out0), .Q(register_1_q), .clk(and_5_out), .clr(Reset));
  Register #(.width(2)) P1 (.D(Priority), .en(decoder_1_out0), .Q(P1_q), .clk(and_5_out));  // open: clr
  Register register_2 (.D(Zone), .en(decoder_1_out1), .Q(register_2_q), .clk(and_5_out), .clr(Reset));
  Register #(.width(2)) P2 (.D(Priority), .en(decoder_1_out1), .Q(P2_q), .clk(and_5_out));  // open: clr
  Register register_3 (.D(Zone), .en(decoder_1_out2), .Q(register_3_q), .clk(and_5_out), .clr(Reset));
  Register #(.width(2)) P3 (.D(Priority), .en(decoder_1_out2), .Q(P3_q), .clk(and_5_out));  // open: clr
  Register register_4 (.D(Zone), .en(decoder_1_out3), .Q(register_4_q), .clk(and_5_out), .clr(Reset));
  Register #(.width(2)) P4 (.D(Priority), .en(decoder_1_out3), .Q(P4_q), .clk(and_5_out));  // open: clr
  Multiplexer #(.select(2), .width(2)) multiplexer_1 (
    .in0(P1_q), .in1(P2_q), .in2(P3_q), .in3(P4_q), .out(out_11), .sel(counter_3_q));  // open: en
  Multiplexer #(.select(2), .width(8)) multiplexer_2 (
    .in0(register_1_q), .in1(register_2_q), .in2(register_3_q), .in3(register_4_q), .out(Output_Zone),
    .sel(counter_3_q));  // open: en
endmodule

// Shelter Full
module Main (
  input  Reset_Queue,
  input  [7:0] in_2,
  input  [1:0] Resource_line,
  input  [7:0] Zone,
  input  in_5,
  input  [1:0] Priority,
  input  [1:0] in_7,
  output [1:0] Output_priority,
  output [7:0] Output_Zone,
  output Shelter_Full,
  output Not_empty,
  output Boost,
  output Food_00,
  output Shelter_01,
  output Evacuation_10,
  output Evac_Empty,
  output Food,
  output Food_Full,
  output Not_empty_2,
  output Boost_2
);

  wire and_1_out, and_2_out, and_3_out, and_4_out, and_6_out, Clock_out, Insert_out, main_1_p1, not_1_out,
       not_2_out, not_3_out, not_4_out, not_5_out, Serve_out;
  wire [1:0] finalselection_1_final_priority, main_1_p11, main_2_priority_2, queue_1_out_11;
  wire [7:0] finalselection_1_final_zone, main_1_p12, main_2_zone_2, queue_1_output_zone;

  not not_1 (not_1_out, Food);
  Decoder #(.select(2)) decoder_1 (
    .out0(Food_00), .out1(Shelter_01), .out2(Evacuation_10), .sel(Resource_line));  // open: out3, en
  Clock Clock (.out(Clock_out));
  Button Insert (.out(Insert_out));
  Button Serve (.out(Serve_out));
  and and_1 (and_1_out, Evac_Empty, not_1_out, Serve_out);
  and and_2 (and_2_out, Serve_out, Food, Evac_Empty);
  not not_2 (not_2_out, Food_00);
  and and_3 (and_3_out, not_4_out, Insert_out, Shelter_01);
  not not_3 (not_3_out, Shelter_01);
  and and_4 (and_4_out, Food_00, Insert_out, not_4_out);
  // Shelter_main main_1: pin names not known; wires that end beside it: main_1_p1, Zone, and_1_out, Priority, Zone, and_3_out, Clock_out, Shelter_Full, Not_empty, Boost, main_1_p11, main_1_p12
  Food_main main_2 (
    .cancel_en(main_1_p1), .Cancel_Zone(Zone), .Serve(and_2_out), .Priority(Priority), .Zone(Zone),
    .Insert(and_4_out), .Clock(Clock_out), .Full(Food_Full), .Valid(Not_empty_2), .Boost(Boost_2),
    .Priority_2(main_2_priority_2), .Zone_2(main_2_zone_2));
  and and_5 (main_1_p1, Evacuation_10, not_3_out, Insert_out, not_2_out);
  not not_4 (not_4_out, main_1_p1);
  Queue queue_1 (
    .Zero(in_2), .Reset(Reset_Queue), .Main_Clock(Clock_out), .Serve(and_6_out), .Insert(main_1_p1),
    .Zone(Zone), .Priority(Priority), .Empty(Evac_Empty), .Output_Zone(queue_1_output_zone),
    .out_11(queue_1_out_11));  // open: Clear
  LED led_1 (.in(1'b1));
  LED led_2 (.in(1'b1));
  not not_5 (not_5_out, Evac_Empty);
  Multiplexer #(.width(8)) multiplexer_1 (
    .in0(queue_1_output_zone), .in1(finalselection_1_final_zone), .out(Output_Zone), .sel(Evac_Empty));  // open: en
  Multiplexer #(.width(2)) multiplexer_2 (
    .in0(queue_1_out_11), .in1(finalselection_1_final_priority), .out(Output_priority), .sel(Evac_Empty));  // open: en
  and and_6 (and_6_out, not_5_out, Serve_out);
  FinalSelection finalselection_1 (
    .in_1(in_2), .in_2(in_5), .Food(Food), .ZoneS(main_1_p12), .PriorityS(main_1_p11), .ValidS(Not_empty),
    .BoostS(Boost), .Priorityf(main_2_priority_2), .ValidF(Not_empty_2), .BoostF(Boost_2),
    .ZoneF(main_2_zone_2), .Serve(1'b1), .in_12(in_7), .Final_Zone(finalselection_1_final_zone),
    .Final_Priority(finalselection_1_final_priority));
  LED led_3 (.in(1'b1));
  LED led_4 (.in(1'b1));
endmodule

// Final Selector
module FinalSelection (
  input  [7:0] in_1,
  input  in_2,
  input  [7:0] ZoneS,
  input  [1:0] PriorityS,
  input  ValidS,
  input  BoostS,
  input  [1:0] Priorityf,
  input  ValidF,
  input  BoostF,
  input  [7:0] ZoneF,
  input  Serve,
  input  [1:0] in_12,
  output [7:0] Final_Zone,
  output Food,
  output [1:0] Final_Priority
);

  wire and_1_out, and_2_out, and_3_out, and_4_out, and_5_out, and_6_out, comparator_1_lt, not_1_out,
       not_2_out, not_3_out, not_4_out, not_5_out, or_1_out, Priority_Chk_out;
  wire [1:0] multiplexer_5_out, multiplexer_7_out, multiplexer_9_out;
  wire [2:0] Show_out;
  wire [7:0] multiplexer_4_out, multiplexer_6_out, multiplexer_8_out;

  Multiplexer #(.select(3)) multiplexer_1 (
    .in0(in_2), .in1(and_1_out), .in3(and_4_out), .in4(in_2), .in7(and_6_out), .out(Food), .sel(Show_out));  // open: in2, in5, in6, en
  or or_1 (or_1_out, ValidS, ValidF);
  and Show (Show_out[0], or_1_out, Serve);
  Multiplexer #(.select(3), .width(8)) multiplexer_2 (
    .in0(in_1), .in1(multiplexer_4_out), .in3(multiplexer_6_out), .in4(in_1), .in7(multiplexer_8_out),
    .out(Final_Zone), .sel(Show_out));  // open: in2, in5, in6, en
  and Valid_Chk (Show_out[1], ValidS, Show_out[0], ValidF);
  not not_1 (not_1_out, Show_out[1]);
  and and_1 (and_1_out, and_2_out, ValidF);
  Multiplexer #(.select(3), .width(2)) multiplexer_3 (
    .in0(in_12), .in1(multiplexer_5_out), .in3(multiplexer_7_out), .in4(in_12), .in7(multiplexer_9_out),
    .out(Final_Priority), .sel(Show_out));  // open: in2, in5, in6, en
  Multiplexer #(.width(8)) multiplexer_4 (
    .in0(ZoneS), .in1(ZoneF), .out(multiplexer_4_out), .sel(and_1_out));  // open: en
  and and_2 (and_2_out, not_1_out, Serve);
  Multiplexer #(.width(2)) multiplexer_5 (
    .in0(PriorityS), .in1(Priorityf), .out(multiplexer_5_out), .sel(and_1_out));  // open: en
  not not_2 (not_2_out, BoostS);
  and Priority_Chk (Priority_Chk_out, BoostS, Show_out[1], BoostF);
  not not_3 (not_3_out, BoostF);
  or or_2 (Show_out[2], Priority_Chk_out, and_3_out);
  and and_3 (and_3_out, not_2_out, Show_out[1], not_5_out, not_3_out);
  not not_4 (not_4_out, Priority_Chk_out);
  and and_4 (and_4_out, and_5_out, BoostF);
  Multiplexer #(.width(8)) multiplexer_6 (
    .in0(ZoneS), .in1(ZoneF), .out(multiplexer_6_out), .sel(and_4_out));  // open: en
  Comparator #(.width(2), .mode("unsigned")) comparator_1 (
    .a(PriorityS), .b(Priorityf), .lt(comparator_1_lt));  // open: gt, eq
  and and_5 (and_5_out, not_4_out, Serve);
  not not_5 (not_5_out, Priority_Chk_out);
  Multiplexer #(.width(2)) multiplexer_7 (
    .in0(PriorityS), .in1(Priorityf), .out(multiplexer_7_out), .sel(and_4_out));  // open: en
  Multiplexer #(.width(8)) multiplexer_8 (
    .in0(ZoneS), .in1(ZoneF), .out(multiplexer_8_out), .sel(and_6_out));  // open: en
  and and_6 (and_6_out, comparator_1_lt, Show_out[2]);
  Multiplexer #(.width(2)) multiplexer_9 (
    .in0(PriorityS), .in1(Priorityf), .out(multiplexer_9_out), .sel(and_6_out));  // open: en
endmodule
