// Logisim project Food.circ as structural Verilog: 10 circuits, main circuit main
module main (
  input  cancel_en,
  input  [7:0] Cancel_Zone,
  input  Serve,
  input  [1:0] Priority,
  input  [7:0] Zone,
  input  Insert,
  input  Clock,
  output Full,
  output Valid,
  output Boost,
  output [1:0] Priority_2,
  output [7:0] Zone_2
);

  final_module final_module_1 (
    .Cancel_En(cancel_en), .Cancel_Zone(Cancel_Zone), .Serve(Serve), .Threshold(8'h14),
    .New_Priority(Priority), .New_Zone_Id(Zone), .Insert(Insert), .Clk(Clock), .Queue_Full(Full),
    .To_FSM_Valid(Valid), .To_FSM_Boost(Boost), .To_FSM_Priority(Priority_2), .To_FSM_Zone_Id(Zone_2));
endmodule

module Request_Register (
  input  Clear,
  input  Set_Boost,
  input  Increment_Wait,
  input  [1:0] Priority_In,
  input  [7:0] Zone_Id_In,
  input  Write_En,
  input  Clk,
  output Boost_Out,
  output Valid_Out,
  output [7:0] Waiting_Time_Out,
  output [1:0] Priority_Out,
  output [7:0] Zone_Id_Out
);

  wire and_1_out, and_2_out, and_3_out, not_1_out, or_1_out, or_2_out;
  wire [7:0] adder_1_out, multiplexer_1_out, multiplexer_2_out;

  not not_1 (not_1_out, Clear);
  and and_1 (and_1_out, or_1_out, not_1_out);
  or or_1 (or_1_out, Boost_Out, Set_Boost);
  or or_2 (or_2_out, Valid_Out, Write_En);
  and and_2 (and_2_out, not_1_out, or_2_out);
  D_Flip_Flop Boost_FF (.clk(Clk), .D(and_1_out), .Q(Boost_Out));  // open: Qn, preset, en, reset
  D_Flip_Flop Valid_FF (.clk(Clk), .D(and_2_out), .Q(Valid_Out));  // open: Qn, preset, en, reset
  Register Wait_Time_Reg (.D(multiplexer_2_out), .en(1'b1), .Q(Waiting_Time_Out), .clk(Clk));  // open: clr
  Register #(.width(2)) Priority_Reg (.D(Priority_In), .en(Write_En), .Q(Priority_Out), .clk(Clk));  // open: clr
  Register Zone_Id_Reg (.D(Zone_Id_In), .en(Write_En), .Q(Zone_Id_Out), .clk(Clk));  // open: clr
  Adder adder_1 (.a(Waiting_Time_Out), .b(8'h1), .out(adder_1_out));  // open: cin, cout
  Multiplexer #(.width(8)) multiplexer_1 (
    .in0(Waiting_Time_Out), .in1(adder_1_out), .out(multiplexer_1_out), .sel(and_3_out));  // open: en
  and and_3 (and_3_out, Valid_Out, Increment_Wait);
  Multiplexer #(.width(8)) multiplexer_2 (
    .in0(multiplexer_1_out), .in1({8{1'b0}}), .out(multiplexer_2_out), .sel(Write_En));  // open: en
endmodule

module Threshold_Comparator (
  input  Valid,
  input  [7:0] Threshold,
  input  [7:0] Waiting_Time,
  output Should_Boost
);

  wire comparator_1_eq, comparator_1_gt, or_1_out;

  Comparator #(.mode("unsigned")) comparator_1 (
    .a(Waiting_Time), .b(Threshold), .gt(comparator_1_gt), .eq(comparator_1_eq));  // open: lt
  or or_1 (or_1_out, comparator_1_gt, comparator_1_eq);
  and and_1 (Should_Boost, Valid, or_1_out);
endmodule

module Priority_Encoder (
  input  B_Valid,
  input  B_Boost,
  input  [7:0] B_Waiting_Time,
  input  [1:0] B_Priority,
  input  [7:0] B_Zone_Id,
  input  A_Valid,
  input  A_Boost,
  input  [7:0] A_Waiting_Time,
  input  [1:0] A_Priority,
  input  [7:0] A_Zone_Id,
  output Select_A,
  output Out_Valid,
  output Out_Boost,
  output [7:0] Out_Waiting_Time,
  output [1:0] Out_Priority,
  output [7:0] Out_Zone_Id
);

  wire A_Boost_out, A_Only_out, and_1_out, and_2_out, and_3_out, Both_out, comparator_1_gt, comparator_2_eq,
       comparator_2_gt, Equal_out, not_1_out, not_2_out;

  not not_1 (not_1_out, B_Valid);
  not not_2 (not_2_out, B_Boost);
  and A_Only (A_Only_out, not_1_out, A_Valid);
  and Both (Both_out, A_Valid, B_Valid);
  and u_A_Boost (A_Boost_out, not_2_out, A_Boost);
  xnor Equal (Equal_out, B_Boost, A_Boost);
  Multiplexer multiplexer_1 (.in0(B_Valid), .in1(A_Valid), .out(Out_Valid), .sel(Select_A));  // open: en
  Comparator #(.mode("unsigned")) comparator_1 (
    .a(A_Waiting_Time), .b(B_Waiting_Time), .gt(comparator_1_gt));  // open: eq, lt
  Comparator #(.width(2), .mode("unsigned")) comparator_2 (
    .a(A_Priority), .b(B_Priority), .gt(comparator_2_gt), .eq(comparator_2_eq));  // open: lt
  and and_1 (and_1_out, Both_out, Equal_out, comparator_2_eq, comparator_1_gt);
  and and_2 (and_2_out, Both_out, Equal_out, comparator_2_gt);
  and and_3 (and_3_out, Both_out, A_Boost_out);
  Multiplexer multiplexer_2 (.in0(B_Boost), .in1(A_Boost), .out(Out_Boost), .sel(Select_A));  // open: en
  Multiplexer #(.width(8)) multiplexer_3 (
    .in0(B_Waiting_Time), .in1(A_Waiting_Time), .out(Out_Waiting_Time), .sel(Select_A));  // open: en
  or or_1 (Select_A, A_Only_out, and_3_out, and_1_out, and_2_out);
  Multiplexer #(.width(8)) multiplexer_4 (
    .in0(B_Zone_Id), .in1(A_Zone_Id), .out(Out_Zone_Id), .sel(Select_A));  // open: en
  Multiplexer #(.width(2)) multiplexer_5 (
    .in0(B_Priority), .in1(A_Priority), .out(Out_Priority), .sel(Select_A));  // open: en
endmodule

module Queue_Storage_2 (
  input  [1:0] Selected_Index,
  input  [7:0] Threshold,
  input  Cancel_En,
  input  [7:0] Cancel_Zone,
  input  Serve,
  input  [1:0] New_Priority,
  input  [7:0] New_Zone_Id,
  input  Insert,
  input  Clk,
  output Queue_Full,
  output Entry3_Valid,
  output Entry3_Boost,
  output [7:0] Entry3_Waiting_Time,
  output [1:0] Entry3_Priority,
  output [7:0] Entry3_Zone_Id,
  output Entry2_Valid,
  output Entry2_Boost,
  output [7:0] Entry2_Waiting_Time,
  output [1:0] Entry2_Priority,
  output [7:0] Entry2_Zone_Id,
  output Entry1_Valid,
  output Entry1_Boost,
  output [7:0] Entry1_Waiting_Time,
  output [1:0] Entry1_Priority,
  output [7:0] Entry1_Zone_Id,
  output Entry0_Valid,
  output Entry0_Boost,
  output [7:0] Entry0_Waiting_Time,
  output [1:0] Entry0_Priority,
  output [7:0] Entry0_Zone_Id
);

  wire and_2_out, and_3_out, and_4_out, and_5_out, and_6_out, and_7_out, and_8_out, and_9_out,
       comparator_1_eq, comparator_2_eq, comparator_3_eq, comparator_4_eq, not_1_out, not_2_out, not_3_out,
       not_4_out, or_1_out, or_2_out, or_3_out, or_4_out, serve_decoder_1_serve_0, serve_decoder_1_serve_1,
       serve_decoder_1_serve_2, serve_decoder_1_serve_3, threshold_comparator_1_should_boost,
       threshold_comparator_2_should_boost, threshold_comparator_3_should_boost,
       threshold_comparator_4_should_boost;

  Request_Register Reg_3 (
    .Clear(or_1_out), .Set_Boost(threshold_comparator_1_should_boost), .Increment_Wait(1'b1),
    .Priority_In(New_Priority), .Zone_Id_In(New_Zone_Id), .Write_En(and_2_out), .Clk(Clk),
    .Boost_Out(Entry3_Boost), .Valid_Out(Entry3_Valid), .Waiting_Time_Out(Entry3_Waiting_Time),
    .Priority_Out(Entry3_Priority), .Zone_Id_Out(Entry3_Zone_Id));
  Request_Register Reg_2 (
    .Clear(or_2_out), .Set_Boost(threshold_comparator_2_should_boost), .Increment_Wait(1'b1),
    .Priority_In(New_Priority), .Zone_Id_In(New_Zone_Id), .Write_En(and_3_out), .Clk(Clk),
    .Boost_Out(Entry2_Boost), .Valid_Out(Entry2_Valid), .Waiting_Time_Out(Entry2_Waiting_Time),
    .Priority_Out(Entry2_Priority), .Zone_Id_Out(Entry2_Zone_Id));
  Request_Register Reg_1 (
    .Clear(or_3_out), .Set_Boost(threshold_comparator_3_should_boost), .Increment_Wait(1'b1),
    .Priority_In(New_Priority), .Zone_Id_In(New_Zone_Id), .Write_En(and_4_out), .Clk(Clk),
    .Boost_Out(Entry1_Boost), .Valid_Out(Entry1_Valid), .Waiting_Time_Out(Entry1_Waiting_Time),
    .Priority_Out(Entry1_Priority), .Zone_Id_Out(Entry1_Zone_Id));
  Request_Register Reg_0 (
    .Clear(or_4_out), .Set_Boost(threshold_comparator_4_should_boost), .Increment_Wait(1'b1),
    .Priority_In(New_Priority), .Zone_Id_In(New_Zone_Id), .Write_En(and_5_out), .Clk(Clk),
    .Boost_Out(Entry0_Boost), .Valid_Out(Entry0_Valid), .Waiting_Time_Out(Entry0_Waiting_Time),
    .Priority_Out(Entry0_Priority), .Zone_Id_Out(Entry0_Zone_Id));
  not not_1 (not_1_out, Entry3_Valid);
  not not_2 (not_2_out, Entry2_Valid);
  not not_3 (not_3_out, Entry1_Valid);
  not not_4 (not_4_out, Entry0_Valid);
  and and_1 (Queue_Full, Entry3_Valid, Entry2_Valid, Entry1_Valid, Entry0_Valid);
  and and_2 (and_2_out, Insert, Entry2_Valid, Entry1_Valid, Entry0_Valid, not_1_out);
  and and_3 (and_3_out, Insert, Entry1_Valid, Entry0_Valid, not_2_out);
  and and_4 (and_4_out, Insert, Entry0_Valid, not_3_out);
  and and_5 (and_5_out, Insert, not_4_out);
  Threshold_Comparator threshold_comparator_1 (
    .Valid(Entry3_Valid), .Threshold(Threshold), .Waiting_Time(Entry3_Waiting_Time),
    .Should_Boost(threshold_comparator_1_should_boost));
  Comparator #(.mode("unsigned")) comparator_1 (
    .a(Entry3_Zone_Id), .b(Cancel_Zone), .eq(comparator_1_eq));  // open: gt, lt
  Threshold_Comparator threshold_comparator_2 (
    .Valid(Entry2_Valid), .Threshold(Threshold), .Waiting_Time(Entry2_Waiting_Time),
    .Should_Boost(threshold_comparator_2_should_boost));
  Comparator #(.mode("unsigned")) comparator_2 (
    .a(Entry2_Zone_Id), .b(Cancel_Zone), .eq(comparator_2_eq));  // open: gt, lt
  Threshold_Comparator threshold_comparator_3 (
    .Valid(Entry1_Valid), .Threshold(Threshold), .Waiting_Time(Entry1_Waiting_Time),
    .Should_Boost(threshold_comparator_3_should_boost));
  Comparator #(.mode("unsigned")) comparator_3 (
    .a(Entry1_Zone_Id), .b(Cancel_Zone), .eq(comparator_3_eq));  // open: gt, lt
  Threshold_Comparator threshold_comparator_4 (
    .Valid(Entry0_Valid), .Threshold(Threshold), .Waiting_Time(Entry0_Waiting_Time),
    .Should_Boost(threshold_comparator_4_should_boost));
  Comparator #(.mode("unsigned")) comparator_4 (
    .a(Entry0_Zone_Id), .b(Cancel_Zone), .eq(comparator_4_eq));  // open: gt, lt
  and and_6 (and_6_out, Cancel_En, comparator_1_eq);
  and and_7 (and_7_out, Cancel_En, comparator_2_eq);
  Serve_Decoder serve_decoder_1 (
    .Selected_Index(Selected_Index), .Serve(Serve), .Serve_3(serve_decoder_1_serve_3),
    .Serve_2(serve_decoder_1_serve_2), .Serve_1(serve_decoder_1_serve_1), .Serve_0(serve_decoder_1_serve_0));
  and and_8 (and_8_out, Cancel_En, comparator_3_eq);
  and and_9 (and_9_out, Cancel_En, comparator_4_eq);
  or or_1 (or_1_out, serve_decoder_1_serve_3, and_6_out);
  or or_2 (or_2_out, serve_decoder_1_serve_2, and_7_out);
  or or_3 (or_3_out, serve_decoder_1_serve_1, and_8_out);
  or or_4 (or_4_out, serve_decoder_1_serve_0, and_9_out);
endmodule

module Serve_Decoder (
  input  [1:0] Selected_Index,
  input  Serve,
  output Serve_3,
  output Serve_2,
  output Serve_1,
  output Serve_0
);

  wire not_1_out, not_2_out;

  not not_1 (not_1_out, Selected_Index[0]);
  not not_2 (not_2_out, Selected_Index[1]);
  and and_1 (Serve_3, Selected_Index[0], Selected_Index[1], Serve);
  and and_2 (Serve_2, not_1_out, Selected_Index[1], Serve);
  and and_3 (Serve_1, Selected_Index[0], not_2_out, Serve);
  and and_4 (Serve_0, not_2_out, not_1_out, Serve);
endmodule

module Priority_Selector_Tree (
  input  Entry3_Valid,
  input  Entry3_Boost,
  input  [7:0] Entry3_Waiting_Time,
  input  [1:0] Entry3_Priority,
  input  [7:0] Entry3_Zone_Id,
  input  Entry2_Valid,
  input  Entry2_Boost,
  input  [7:0] Entry2_Waiting_Time,
  input  [1:0] Entry2_Priority,
  input  [7:0] Entry2_Zone_Id,
  input  Entry1_Valid,
  input  Entry1_Boost,
  input  [7:0] Entry1_Waiting_Time,
  input  [1:0] Entry1_Priority,
  input  [7:0] Entry1_Zone_Id,
  input  Entry0_Valid,
  input  Entry0_Boost,
  input  [7:0] Entry0_Waiting_Time,
  input  [1:0] Entry0_Priority,
  input  [7:0] Entry0_Zone_Id,
  output [1:0] Selected_Index,
  output Selected_Valid,
  output Selected_Boost,
  output [7:0] Selected_Waiting_Time,
  output [1:0] Selected_Priority,
  output [7:0] Selected_Zone_Id
);

  wire Comp_0_1_out_boost, Comp_0_1_out_valid, Comp_0_1_select_a, Comp_2_3_out_boost, Comp_2_3_out_valid,
       Comp_2_3_select_a, Comp_Final_select_a;
  wire [1:0] Comp_0_1_out_priority, Comp_2_3_out_priority, multiplexer_1_out, multiplexer_2_out;
  wire [7:0] Comp_0_1_out_waiting_time, Comp_0_1_out_zone_id, Comp_2_3_out_waiting_time, Comp_2_3_out_zone_id;

  Priority_Encoder Comp_2_3 (
    .B_Valid(Entry3_Valid), .B_Boost(Entry3_Boost), .B_Waiting_Time(Entry3_Waiting_Time),
    .B_Priority(Entry3_Priority), .B_Zone_Id(Entry3_Zone_Id), .A_Valid(Entry2_Valid), .A_Boost(Entry2_Boost),
    .A_Waiting_Time(Entry2_Waiting_Time), .A_Priority(Entry2_Priority), .A_Zone_Id(Entry2_Zone_Id),
    .Select_A(Comp_2_3_select_a), .Out_Valid(Comp_2_3_out_valid), .Out_Boost(Comp_2_3_out_boost),
    .Out_Waiting_Time(Comp_2_3_out_waiting_time), .Out_Priority(Comp_2_3_out_priority),
    .Out_Zone_Id(Comp_2_3_out_zone_id));
  Priority_Encoder Comp_0_1 (
    .B_Valid(Entry1_Valid), .B_Boost(Entry1_Boost), .B_Waiting_Time(Entry1_Waiting_Time),
    .B_Priority(Entry1_Priority), .B_Zone_Id(Entry1_Zone_Id), .A_Valid(Entry0_Valid), .A_Boost(Entry0_Boost),
    .A_Waiting_Time(Entry0_Waiting_Time), .A_Priority(Entry0_Priority), .A_Zone_Id(Entry0_Zone_Id),
    .Select_A(Comp_0_1_select_a), .Out_Valid(Comp_0_1_out_valid), .Out_Boost(Comp_0_1_out_boost),
    .Out_Waiting_Time(Comp_0_1_out_waiting_time), .Out_Priority(Comp_0_1_out_priority),
    .Out_Zone_Id(Comp_0_1_out_zone_id));
  Multiplexer #(.width(2)) multiplexer_1 (
    .in0(2'b11), .in1(2'b10), .out(multiplexer_1_out), .sel(Comp_2_3_select_a));  // open: en
  Multiplexer #(.width(2)) multiplexer_2 (
    .in0(2'b01), .in1(2'b00), .out(multiplexer_2_out), .sel(Comp_0_1_select_a));  // open: en
  Priority_Encoder Comp_Final (
    .B_Valid(Comp_2_3_out_valid), .B_Boost(Comp_2_3_out_boost), .B_Waiting_Time(Comp_2_3_out_waiting_time),
    .B_Priority(Comp_2_3_out_priority), .B_Zone_Id(Comp_2_3_out_zone_id), .A_Valid(Comp_0_1_out_valid),
    .A_Boost(Comp_0_1_out_boost), .A_Waiting_Time(Comp_0_1_out_waiting_time),
    .A_Priority(Comp_0_1_out_priority), .A_Zone_Id(Comp_0_1_out_zone_id), .Select_A(Comp_Final_select_a),
    .Out_Valid(Selected_Valid), .Out_Boost(Selected_Boost), .Out_Waiting_Time(Selected_Waiting_Time),
    .Out_Priority(Selected_Priority), .Out_Zone_Id(Selected_Zone_Id));
  Multiplexer #(.width(2)) multiplexer_3 (
    .in0(multiplexer_1_out), .in1(multiplexer_2_out), .out(Selected_Index), .sel(Comp_Final_select_a));  // open: en
endmodule

module final_module (
  input  Cancel_En,
  input  [7:0] Cancel_Zone,
  input  Serve,
  input  [7:0] Threshold,
  input  [1:0] New_Priority,
  input  [7:0] New_Zone_Id,
  input  Insert,
  input  Clk,
  output Queue_Full,
  output To_FSM_Valid,
  output To_FSM_Boost,
  output [1:0] To_FSM_Priority,
  output [7:0] To_FSM_Zone_Id
);

  wire Queue_entry0_boost, Queue_entry0_valid, Queue_entry1_boost, Queue_entry1_valid, Queue_entry2_boost,
       Queue_entry2_valid, Queue_entry3_boost, Queue_entry3_valid;
  wire [1:0] Queue_entry0_priority, Queue_entry1_priority, Queue_entry2_priority, Queue_entry3_priority,
       Selector_selected_index;
  wire [7:0] Queue_entry0_waiting_time, Queue_entry0_zone_id, Queue_entry1_waiting_time,
       Queue_entry1_zone_id, Queue_entry2_waiting_time, Queue_entry2_zone_id, Queue_entry3_waiting_time,
       Queue_entry3_zone_id;

  Queue_Storage_2 Queue (
    .Selected_Index(Selector_selected_index), .Threshold(Threshold), .Cancel_En(Cancel_En),
    .Cancel_Zone(Cancel_Zone), .Serve(Serve), .New_Priority(New_Priority), .New_Zone_Id(New_Zone_Id),
    .Insert(Insert), .Clk(Clk), .Queue_Full(Queue_Full), .Entry3_Valid(Queue_entry3_valid),
    .Entry3_Boost(Queue_entry3_boost), .Entry3_Waiting_Time(Queue_entry3_waiting_time),
    .Entry3_Priority(Queue_entry3_priority), .Entry3_Zone_Id(Queue_entry3_zone_id),
    .Entry2_Valid(Queue_entry2_valid), .Entry2_Boost(Queue_entry2_boost),
    .Entry2_Waiting_Time(Queue_entry2_waiting_time), .Entry2_Priority(Queue_entry2_priority),
    .Entry2_Zone_Id(Queue_entry2_zone_id), .Entry1_Valid(Queue_entry1_valid),
    .Entry1_Boost(Queue_entry1_boost), .Entry1_Waiting_Time(Queue_entry1_waiting_time),
    .Entry1_Priority(Queue_entry1_priority), .Entry1_Zone_Id(Queue_entry1_zone_id),
    .Entry0_Valid(Queue_entry0_valid), .Entry0_Boost(Queue_entry0_boost),
    .Entry0_Waiting_Time(Queue_entry0_waiting_time), .Entry0_Priority(Queue_entry0_priority),
    .Entry0_Zone_Id(Queue_entry0_zone_id));
  Priority_Selector_Tree Selector (
    .Entry3_Valid(Queue_entry3_valid), .Entry3_Boost(Queue_entry3_boost),
    .Entry3_Waiting_Time(Queue_entry3_waiting_time), .Entry3_Priority(Queue_entry3_priority),
    .Entry3_Zone_Id(Queue_entry3_zone_id), .Entry2_Valid(Queue_entry2_valid),
    .Entry2_Boost(Queue_entry2_boost), .Entry2_Waiting_Time(Queue_entry2_waiting_time),
    .Entry2_Priority(Queue_entry2_priority), .Entry2_Zone_Id(Queue_entry2_zone_id),
    .Entry1_Valid(Queue_entry1_valid), .Entry1_Boost(Queue_entry1_boost),
    .Entry1_Waiting_Time(Queue_entry1_waiting_time), .Entry1_Priority(Queue_entry1_priority),
    .Entry1_Zone_Id(Queue_entry1_zone_id), .Entry0_Valid(Queue_entry0_valid),
    .Entry0_Boost(Queue_entry0_boost), .Entry0_Waiting_Time(Queue_entry0_waiting_time),
    .Entry0_Priority(Queue_entry0_priority), .Entry0_Zone_Id(Queue_entry0_zone_id),
    .Selected_Index(Selector_selected_index), .Selected_Valid(To_FSM_Valid), .Selected_Boost(To_FSM_Boost),
    .Selected_Priority(To_FSM_Priority), .Selected_Zone_Id(To_FSM_Zone_Id));  // open: Selected_Waiting_Time
endmodule

module Incoming (
  input  [1:0] Resource_line,
  input  [7:0] Zone,
  input  [1:0] Priority,
  output Full,
  output Valid,
  output Boost,
  output Food_00,
  output Shelter_01,
  output Evacuation_10,
  output [7:0] Output_Zone,
  output [1:0] Zone_priority
);

  wire and_1_out, and_2_out, Cancel_out, Clock_out, Insert_out, not_1_out, not_2_out, not_3_out, Serve_out;

  Decoder #(.select(2)) decoder_1 (
    .out0(Food_00), .out1(Shelter_01), .out2(Evacuation_10), .sel(Resource_line));  // open: out3, en
  Clock Clock (.out(Clock_out));
  Button Insert (.out(Insert_out));
  Button Serve (.out(Serve_out));
  Button Cancel (.out(Cancel_out));
  not not_1 (not_1_out, Food_00);
  and and_1 (and_1_out, not_3_out, Insert_out, Shelter_01);
  not not_2 (not_2_out, Shelter_01);
  main main_1 (
    .cancel_en(Cancel_out), .Cancel_Zone(Zone), .Serve(Serve_out), .Priority(Priority), .Zone(Zone),
    .Insert(and_1_out), .Clock(Clock_out), .Full(Full), .Valid(Valid), .Boost(Boost),
    .Priority_2(Zone_priority), .Zone_2(Output_Zone));
  and and_2 (and_2_out, Evacuation_10, not_2_out, not_1_out);
  not not_3 (not_3_out, and_2_out);
endmodule

module test (
  input  in_1,
  input  [7:0] in_2,
  input  [1:0] in_3,
  input  [7:0] in_4,
  input  in_5,
  input  in_6,
  input  in_7,
  output Waiting_Tine_Out,
  output Waiting_Tine_Out_2,
  output [7:0] Waiting_Tine_Out_3,
  output Waiting_Tine_Out_4,
  output [1:0] Waiting_Tine_Out_5
);

  main main_1 (
    .cancel_en(in_1), .Cancel_Zone(in_2), .Serve(in_6), .Priority(in_3), .Zone(in_4), .Insert(in_5),
    .Clock(in_7), .Full(Waiting_Tine_Out), .Valid(Waiting_Tine_Out_2), .Boost(Waiting_Tine_Out_4),
    .Priority_2(Waiting_Tine_Out_5), .Zone_2(Waiting_Tine_Out_3));
endmodule
